// Logisim project ALU.circ as structural Verilog
module my_adder (
  input  A,
  input  SUM,
  input  B,
  input  CARRY
);

  xor xor_1 (SUM, A, B);
  and and_1 (CARRY, A, B);
endmodule
